# Fritzing sketch RFID board (saved by Fritzing 0.9.2b)
breadboards: 1

parts:
  R1 = Resistor [tolerance=±5% resistance=220 package=THT]
  R2 = Resistor [tolerance=±5% resistance=220 package=THT]
  R3 = Resistor [tolerance=±5% resistance=220 package=THT]
  LED1 = LED - 5mm [color="Red (633nm)" package="5 mm [THT]"]
  LED2 = LED - 5mm [color="Red (633nm)" package="5 mm [THT]"]
  LED3 = LED - 5mm [color="Green (570nm)" package="5 mm [THT]"]
  LED4 = LED - 5mm [color="Green (570nm)" package="5 mm [THT]"]
  LED5 = LED - 5mm [color="Orange (620nm)" package="5 mm [THT]"]
  LED6 = LED - 5mm [color="Orange (620nm)" package="5 mm [THT]"]
  Part1 = Arduino Uno (Rev3)
  RFID1 = RFID Reader
  ANT1 = Antenna

nets:
  N1: R1.Pin_0, Part1.D7
  N2: R1.Pin_1, LED1.cathode, LED2.anode, LED3.cathode, LED4.cathode
  N3: R2.Pin_0, Part1.D6_PWM
  N4: R2.Pin_1, LED1.anode, LED2.cathode, LED5.cathode, LED6.cathode
  N5: R3.Pin_0, Part1.D5_PWM
  N6: R3.Pin_1, LED3.anode, LED4.anode, LED5.anode, LED6.anode
  N7: Part1.D9_PWM, RFID1.RES
  N8: Part1.D10_PWM/SS, RFID1.ANT0
  N9: Part1.D11_PWM/MOSI, RFID1.D0
  N10: Part1.D12/MISO, RFID1.D1
  N11: Part1.D13/SCK, RFID1.Future
  3V3: Part1.3V3, RFID1.+5V
  GND: Part1.GND, RFID1.GND
  N12: RFID1.ANT1, RFID1.CP, ANT1.antenna_lead
